# Fritzing sketch BeaconScanner (saved by Fritzing 0.9.2b)
circuit board: 8.46667cm x 5.64444cm
breadboards: 1

parts:
  Raspberry_Pi1 = Raspberry Pi B rev2
  LCD1 = LCD screen
  R1 = Trimmer Potentiometer [maximum_resistance=10kΩ package=THT]
  S1 = Pushbutton [package=THT]

nets:
  5V: Raspberry_Pi1.5V, LCD1.VDD, LCD1.LED+
  GND: Raspberry_Pi1.GND, LCD1.VSS, LCD1.R/W, LCD1.LED-, S1.leg0
  N1: Raspberry_Pi1.GPIO_23, LCD1.DB4
  N2: Raspberry_Pi1.GPIO_17, S1.leg1
  N3: Raspberry_Pi1.GPIO_4, LCD1.DB7
  N4: Raspberry_Pi1.GPIO_24, LCD1.DB5
  N5: Raspberry_Pi1.GPIO_25, LCD1.DB6
  N6: Raspberry_Pi1.GPIO_7, LCD1.DB0
  N7: LCD1.V0, R1.wiper
